# Fritzing sketch Laser_Driver (saved by Fritzing 0.9.3b)
perfboards: 1

parts:
  U1 = IC, DIP package, 14 pins [chip_label=IC]
  R1 = Resistor [tolerance=±5% resistance=100 package=THT]
  R2 = Resistor [tolerance=±5% resistance=100 package=THT]
  R3 = Resistor [tolerance=±5% resistance=100 package=THT]
  Q1 = NPN-Transistor [package="TO92 [THT]"]
  LD1 = LD
  R4 = Resistor [tolerance=±5% resistance=1k package=THT]

nets:
  N1: U1.pin1, Q1.B
  N2: U1.pin2, R1.Pin_1
  N3: U1.pin3, U1.pin4, Q1.C
  N4: U1.pin11, R4.Pin_0
  N5: R1.Pin_0, R2.Pin_1
  N6: R2.Pin_0, R3.Pin_1
  N7: R3.Pin_0, LD1.cathode, R4.Pin_1
  N8: Q1.E, LD1.anode

custom parts:
  LD: A Generic Red Dot Laser Diode Module (~5mW)
