# Fritzing sketch PWM_averager (saved by Fritzing 0.9.3b)
circuit board: 8.46667cm x 5.64444cm
perfboards: 1

parts:
  R1 = Resistor [tolerance=±5% resistance=100 package=THT]
  Q1 = TRANSISTOR_NPN [package=to-92-ammo]
  R2 = Resistor [tolerance=±5% resistance=1k package=THT]
  J1 = female pin header, 2 pins [form="♀ (female)"]
  Q2 = TRANSISTOR_NPN [package=to-92-ammo]
  C1 = Capacitor Polarized [package=cpol-radial-100uf-25v]
  R3 = Resistor [tolerance=±5% resistance=470 package=THT]
  J2 = female pin header, 3 pins [form="♀ (female)"]

nets:
  N1: R1.Pin_0, J2.pin2
  N2: R1.Pin_1, Q1.B
  N3: Q1.E, C1.+, R3.Pin_0
  N4: Q1.C, R2.Pin_0
  N5: R2.Pin_1, J1.pin1, J2.pin3
  N6: J1.pin2, Q2.C
  N7: Q2.E, C1.-, J2.pin1
  N8: Q2.B, R3.Pin_1
