# Fritzing sketch full_schem (saved by Fritzing 0.9.3b)
breadboards: 1

parts:
  U2 = IC, DIP package, 14 pins [chip_label=LF347n]
  R5 = Resistor [tolerance=±5% resistance=1k package=THT]
  R6 = Resistor [tolerance=±5% resistance=100 package=THT]
  R7 = Resistor [tolerance=±5% resistance=100 package=THT]
  R8 = Resistor [tolerance=±5% resistance=100 package=THT]
  Q1 = NPN-Transistor [package="TO92 [THT]"]
  LD1 = LD
  R9 = Resistor [tolerance=±5% resistance=470 package=THT]
  R2 = Resistor [tolerance=±5% resistance=1k package=THT]
  R1 = Resistor [tolerance=±5% resistance=100 package=THT]
  Q3 = TRANSISTOR_NPN [package=to-92-ammo]
  Q2 = TRANSISTOR_NPN [package=to-92-ammo]
  C1 = Capacitor Polarized [part_number=10uF package=cpol-radial-100uf-25v]
  U1 = Arduino Nano (Rev3.0)
  X-axis = Loudspeaker
  Power_Control = female pin header, 1 pin [form="♀ (female)"]
  S1 = Momentary Switch [package=ksa_sealed_tac_switch]
  U3 = L298_BRIDGE_DRIVER [package=powerso20]
  L2 = Solenoid
  L1 = Solenoid
  R4 = Resistor [tolerance=±5% resistance=100 package=THT]
  R3 = Resistor [tolerance=±5% resistance=100 package=THT]

nets:
  N1: U2.pin1, Q1.B
  N2: U2.pin2, R8.Pin_1
  5V: U2.pin3, U2.pin4, Q1.C, R2.Pin_1
  GND: U2.pin11, R5.Pin_0, Q3.E, C1.-, U1.GND, S1.3, S1.4, U3.GND
  N3: R5.Pin_1, R6.Pin_0, LD1.cathode, U1.A4
  N4: R6.Pin_1, R7.Pin_0
  N5: R7.Pin_1, R8.Pin_0
  N6: Q1.E, LD1.anode
  N7: R9.Pin_0, Q2.E, C1.+
  N8: R9.Pin_1, Q3.B
  N9: R2.Pin_0, Q2.C
  N10: R1.Pin_0, U1.D6
  N11: R1.Pin_1, Q2.B
  N12: Q3.C, X-axis.pin2
  N13: U1.D3, U3.IN2
  N14: U1.D4, Power_Control.pin1, S1.1, S1.2
  N15: U1.D9, U3.IN3
  N16: U1.D10, U3.IN1
  N17: U1.D11/MOSI, U3.IN4
  5V_2: U1.5V, U3.ENA, U3.VSS, U3.ENB
  N18: X-axis.pin1, U3.VS
  N19: U3.OUT1, L1.pin1
  N20: U3.OUT2, R3.Pin_0
  N21: U3.OUT3, L2.pin2
  N22: U3.OUT4, R4.Pin_1
  N23: L2.pin1, R4.Pin_0
  N24: L1.pin2, R3.Pin_1

notes:
  Home-built TLSM, A transmission-mode laser scanning microscope made with common and salvaged parts, 1.1

custom parts:
  LD: A Generic Red Dot Laser Diode Module (~5mW)
